# Fritzing sketch RFID_Project (saved by Fritzing 0.9.3b)
breadboards: 2

parts:
  Orange_Pi_One1 = Orange Pi One [part_number=OPI-ONE]
  KY-1 = Keyes Relay [package=THT]
  Part1 = RFID-RC522-v3
  L1 = Solenoid
  M1 = RioRand LM2596
  LED1 = LED - 5mm [color="Green (565nm)" package="5 mm [THT]"]
  LED2 = LED - 5mm [color="Red (633nm)" package="5 mm [THT]"]
  R1 = Resistor [tolerance=±5% resistance=220 package=THT]
  R2 = Resistor [tolerance=±5% resistance=220 package=THT]
  JACK1 = 2.1mm Barrel Jack with Terminal Block
  LED4 = LED - 5mm [color="Red (633nm)" package="5 mm [THT]"]
  LED5 = LED - 5mm [color="Green (565nm)" package="5 mm [THT]"]
  S2 = Round Pushbutton
  R4 = Resistor [tolerance=±5% resistance=220 package=THT]
  R5 = Resistor [tolerance=±5% resistance=220 package=THT]
  R6 = Resistor [tolerance=±5% resistance=220 package=THT]

nets:
  3V3: Orange_Pi_One1.3v3, Orange_Pi_One1.3V3, Part1.3.3V, R6.Pin_1
  N1: Orange_Pi_One1.PA12, R2.Pin_0
  N2: Orange_Pi_One1.PA11, R1.Pin_0
  N3: Orange_Pi_One1.PA6, KY-1.signal
  GND: Orange_Pi_One1.GND, KY-1.ground, Part1.GND, M1.Pin_4, LED1.cathode, LED2.cathode, LED4.cathode, LED5.cathode, S2.leg0
  N4: Orange_Pi_One1.PA14, S2.leg1, R6.Pin_0
  N5: Orange_Pi_One1.PA1, R5.Pin_0
  N6: Orange_Pi_One1.PA0, R4.Pin_0
  N7: Orange_Pi_One1.PC0, Part1.MISO
  N8: Orange_Pi_One1.PC1, Part1.MOSI
  N9: Orange_Pi_One1.PC2, Part1.SCK
  N10: Orange_Pi_One1.PC3, Part1.SDA
  N11: Orange_Pi_One1.PA19, Part1.RST
  N12: Orange_Pi_One1.PA7, Part1.IRQ
  N13: Orange_Pi_One1.5V, KY-1.power, M1.Pin_3
  N14: KY-1.C, L1.pin2
  N15: KY-1.NO, M1.Pin_1, JACK1.POS
  N16: L1.pin1, M1.Pin_2, JACK1.NEG
  N17: LED1.anode, R2.Pin_1
  N18: LED2.anode, R1.Pin_1
  N19: LED4.anode, R4.Pin_1
  N20: LED5.anode, R5.Pin_1

notes:
  Door Lock
  Input 12V DC
  Door
  Button
  RFID Cards Reader
  System Status LEDS
  DC/DC 5V
  Relay
  Lock state LEDS
  PINOUT TABLE:
  PA12 - DOOR GREEN LED
  PA11 - DOOR RED LED
  PA6 - LOCK RELAY
  PA14 - DOOR BUTTON
  PA1 - SYSTEM GREEN LED
  PA0 - SYSTEM RED LED
  PC0 - RC522 MISI
  PC1 - RC522 MOSO
  PC2 - RC522 SCK
  PC3 - RC522 CS
  PA19 - RC522 RESET
  PA7 - RC522 IRQ

custom parts:
  Orange Pi One: It’s an open-source single-board computer. It can run Android 4.4, Ubuntu, Debian, Rasberry Pi Image, as well as the banana pi Image. It uses the AllWinner H3 SoC, and has 512MB DDR3 SDRAM
  Keyes Relay: The Keyes 5V relay module is suitable for SCM development, home appliance control. It uses a 5V~12V TIL control signal which can control DC / AC signal.
  RFID-RC522-v3: A simple China made RFID-RC522 Reader (6x4 cm); do check the pin labels, as this is a MFRC522 based clone.
